# Fritzing sketch design (saved by Fritzing 1.0.2b)
breadboards: 1

parts:
  Nano2 = Arduino Nano v2.3
  Part1 = HX711 Weighing Sensor Module
  LCD2 = LCD screen
  LCM1602_IIC2 = LCM1602 IIC [part_number="LCM1602 IIC" chip_label="LCM1602 IIC" package="DIP (Dual Inline) [THT]"]
  S1 = Load Sensor - 50kg [part_number=SEN-10245]
  S2 = Load Sensor - 50kg [part_number=SEN-10245]
  S3 = Load Sensor - 50kg [part_number=SEN-10245]
  S4 = Load Sensor - 50kg [part_number=SEN-10245]

nets:
  N1: Nano2.RST, LCM1602_IIC2.GND
  GND: Nano2.GND, Part1.GND, Part1.DO/RX
  N2: Nano2.D2, Part1.CK/TX
  VCC: Nano2.+5V, Part1.VCC, LCM1602_IIC2.VCC
  N3: Part1.E+, S1.R
  N4: Part1.E-, S3.R
  N5: Part1.A+, S2.R
  N6: Part1.A-, S4.R
  VSS: LCD2.VSS, LCM1602_IIC2.VSS
  VDD: LCD2.VDD, LCM1602_IIC2.VDD
  N7: LCD2.V0, LCM1602_IIC2.V0
  N8: LCD2.RS, LCM1602_IIC2.RS
  N9: LCD2.R/W, LCM1602_IIC2.RW
  N10: LCD2.E, LCM1602_IIC2.E
  N11: LCD2.DB0, LCM1602_IIC2.D0
  N12: LCD2.DB1, LCM1602_IIC2.D1
  N13: LCD2.DB2, LCM1602_IIC2.D2
  N14: LCD2.DB3, LCM1602_IIC2.D3
  N15: LCD2.DB4, LCM1602_IIC2.D4
  N16: LCD2.DB5, LCM1602_IIC2.D5
  N17: LCD2.DB6, LCM1602_IIC2.D6
  N18: LCD2.DB7, LCM1602_IIC2.D7
  N19: LCD2.LED+, LCM1602_IIC2.A
  N20: LCD2.LED-, LCM1602_IIC2.K
  N21: LCM1602_IIC2.LED_A, LCM1602_IIC2.LED_B
  N22: S1.B, S2.B
  N23: S1.W, S4.W
  N24: S2.W, S3.W
  N25: S3.B, S4.B

custom parts:
  LCM1602 IIC: I2C-Module to use a 1602 or 2004 LCD on with the wire.h libory Serial LCD Modul
  Load Sensor - 50kg: Half-wheatstone bridge Load Cell modified from the Fritzing Repo This load sensor, sometimes called a strain gauge, is the same one found in digital bathroom scales (you know, the ones you use in January for your New Year's resolutions, and then forget about a month later). This sensor can measure up to about 110 pounds.
